# Fritzing sketch SpoolBoard (saved by Fritzing 0.9.4)
circuit board: 6cm x 3cm

parts:
  Pololu_A1 = Pololu A4988 [package=SO16]
  WeMos_D1_Mini1 = WeMos D1 Mini
  M1 = Stepper Motor - Bipolar
  J1 = Dagu DGServo 9g header connector (female) [package=THT]
  S1 = Round Pushbutton
  C1 = Capacitor Polarized [package=panasonic_c]

nets:
  N1: Pololu_A1.RESET, Pololu_A1.SLEEP
  N2: Pololu_A1.STEP, WeMos_D1_Mini1.D5
  N3: Pololu_A1.DIR, WeMos_D1_Mini1.D0
  N4: Pololu_A1.GND#8, WeMos_D1_Mini1.G
  VDD: Pololu_A1.VDD, WeMos_D1_Mini1.5V, S1.leg0
  N5: Pololu_A1.1B, M1.D
  N6: Pololu_A1.1A, M1.B
  N7: Pololu_A1.2A, M1.C
  N8: Pololu_A1.2B, M1.A
  N9: Pololu_A1.GND#14, J1.pulse, C1.-
  N10: Pololu_A1.VMOT, J1.gnd, C1.+
  N11: WeMos_D1_Mini1.D4, S1.leg1
